// Logisim project Track_Counter.circ as structural Verilog: 1 circuit, main circuit main
module main (
  input  in_1
);

  wire and_1_out, and_2_out, and_3_out, and_4_out, and_5_out, and_6_out, and_7_out, and_8_out, and_9_out,
       and_10_out, and_11_out, and_12_out, and_13_out, GreaterThan9ThenChange_out, GreaterThan99Reset_out,
       If0ThenSet1_out, IfGreaterThan99Set1_out, j_k_ff_1_qn, j_k_ff_2_qn, j_k_ff_3_qn, j_k_ff_4_qn,
       j_k_ff_5_qn, j_k_ff_6_qn, LowerThan9NoChange_out, NoGreaterThan9_out, NoLowerThan0_out, nor_1_out,
       nor_2_out, not_1_out, not_2_out, not_3_out, not_4_out, not_5_out, not_6_out, not_7_out, not_8_out,
       not_9_out, not_10_out, not_11_out, not_12_out, or_1_out, or_2_out, or_3_out, or_4_out, or_5_out,
       or_6_out, or_7_out, or_8_out, or_9_out, or_10_out, or_11_out, or_12_out, or_13_out, or_14_out,
       Previous_out, SKip_out;
  wire [3:0] and_14_out, and_15_out, j_k_ff_1_q, j_k_ff_2_q;

  Button SKip (.out(SKip_out));
  Button Previous (.out(Previous_out));
  nor nor_1 (nor_1_out, SKip_out, nor_2_out);
  nor nor_2 (nor_2_out, nor_1_out, Previous_out);
  or or_1 (or_1_out, SKip_out, Previous_out);
  not not_1 (not_1_out, LowerThan9NoChange_out);
  not not_2 (not_2_out, nor_2_out);
  or or_2 (or_2_out, IfGreaterThan99Set1_out, If0ThenSet1_out);
  and and_1 (and_1_out, not_1_out, not_2_out);
  or or_3 (or_3_out, GreaterThan9ThenChange_out, and_1_out);
  J_K_Flip_Flop #(.trigger("falling")) j_k_ff_1 (
    .J(in_1), .K(in_1), .clk(or_1_out), .Q(j_k_ff_1_q[0]), .Qn(j_k_ff_1_qn), .preset(or_2_out),
    .reset(NoGreaterThan9_out));
  not not_3 (not_3_out, nor_2_out);
  J_K_Flip_Flop #(.trigger("falling")) j_k_ff_2 (
    .J(in_1), .K(in_1), .clk(or_3_out), .Q(j_k_ff_2_q[0]), .Qn(j_k_ff_2_qn), .reset(IfGreaterThan99Set1_out));  // open: preset
  not not_4 (not_4_out, nor_2_out);
  and and_2 (and_2_out, nor_2_out, j_k_ff_1_q[0]);
  and and_3 (and_3_out, j_k_ff_1_qn, not_3_out);
  and and_4 (and_4_out, nor_2_out, j_k_ff_2_q[0]);
  and and_5 (and_5_out, j_k_ff_2_qn, not_4_out);
  J_K_Flip_Flop #(.trigger("falling")) j_k_ff_3 (
    .J(or_4_out), .K(or_4_out), .clk(or_1_out), .Q(j_k_ff_1_q[1]), .Qn(j_k_ff_3_qn), .reset(or_5_out));  // open: preset
  or or_4 (or_4_out, and_2_out, and_3_out);
  or or_5 (or_5_out, NoLowerThan0_out, NoGreaterThan9_out);
  J_K_Flip_Flop #(.trigger("falling")) j_k_ff_4 (
    .J(or_6_out), .K(or_6_out), .clk(or_3_out), .Q(j_k_ff_2_q[1]), .Qn(j_k_ff_4_qn), .reset(or_7_out));  // open: preset
  or or_6 (or_6_out, and_4_out, and_5_out);
  or or_7 (or_7_out, GreaterThan99Reset_out, IfGreaterThan99Set1_out);
  and and_6 (and_6_out, and_2_out, j_k_ff_1_q[1]);
  and and_7 (and_7_out, j_k_ff_3_qn, and_3_out);
  and and_8 (and_8_out, and_4_out, j_k_ff_2_q[1]);
  and and_9 (and_9_out, j_k_ff_4_qn, and_5_out);
  J_K_Flip_Flop #(.trigger("falling")) j_k_ff_5 (
    .J(or_8_out), .K(or_8_out), .clk(or_1_out), .Q(j_k_ff_1_q[2]), .Qn(j_k_ff_5_qn), .reset(or_10_out));  // open: preset
  or or_8 (or_8_out, and_6_out, and_7_out);
  J_K_Flip_Flop #(.trigger("falling")) j_k_ff_6 (
    .J(or_9_out), .K(or_9_out), .clk(or_3_out), .Q(j_k_ff_2_q[2]), .Qn(j_k_ff_6_qn), .reset(or_11_out));  // open: preset
  or or_9 (or_9_out, and_8_out, and_9_out);
  or or_10 (or_10_out, NoLowerThan0_out, NoGreaterThan9_out);
  or or_11 (or_11_out, GreaterThan99Reset_out, IfGreaterThan99Set1_out);
  and and_10 (and_10_out, and_6_out, j_k_ff_1_q[2]);
  and and_11 (and_11_out, j_k_ff_5_qn, and_7_out);
  and and_12 (and_12_out, and_8_out, j_k_ff_2_q[2]);
  and and_13 (and_13_out, j_k_ff_6_qn, and_9_out);
  or or_12 (or_12_out, and_10_out, and_11_out);
  or or_13 (or_13_out, and_12_out, and_13_out);
  J_K_Flip_Flop #(.trigger("falling")) j_k_ff_7 (
    .J(or_12_out), .K(or_12_out), .clk(or_1_out), .Q(j_k_ff_1_q[3]), .preset(If0ThenSet1_out),
    .reset(NoGreaterThan9_out));  // open: Qn
  J_K_Flip_Flop #(.trigger("falling")) j_k_ff_8 (
    .J(or_13_out), .K(or_13_out), .clk(or_3_out), .Q(j_k_ff_2_q[3]), .reset(IfGreaterThan99Set1_out));  // open: Qn, preset
  and IfGreaterThan99Set1 (IfGreaterThan99Set1_out, j_k_ff_2_q[3], nor_2_out, j_k_ff_2_q[1]);
  and NoGreaterThan9 (NoGreaterThan9_out, j_k_ff_1_q[3], nor_2_out, j_k_ff_1_q[1]);
  or or_14 (or_14_out, j_k_ff_2_q[1], j_k_ff_2_q[2]);
  and GreaterThan99Reset (GreaterThan99Reset_out, j_k_ff_2_q[3], or_14_out, j_k_ff_2_q[0]);
  and NoLowerThan0 (NoLowerThan0_out, j_k_ff_1_q[3], j_k_ff_1_q[1], j_k_ff_1_q[0]);
  or LowerThan9NoChange (LowerThan9NoChange_out, j_k_ff_1_q[0], j_k_ff_1_q[1], j_k_ff_1_q[2], j_k_ff_1_q[3]);
  and GreaterThan9ThenChange (GreaterThan9ThenChange_out, j_k_ff_1_q[0], nor_2_out, j_k_ff_1_q[3]);
  assign and_14_out = {4{in_1}} & j_k_ff_1_q;  // AND_Gate and_14, 4 bits wide
  not not_5 (not_5_out, j_k_ff_2_q[3]);
  not not_6 (not_6_out, j_k_ff_2_q[2]);
  not not_7 (not_7_out, j_k_ff_2_q[1]);
  not not_8 (not_8_out, j_k_ff_2_q[0]);
  not not_9 (not_9_out, j_k_ff_1_q[3]);
  not not_10 (not_10_out, j_k_ff_1_q[2]);
  not not_11 (not_11_out, j_k_ff_1_q[1]);
  not not_12 (not_12_out, j_k_ff_1_q[0]);
  assign and_15_out = j_k_ff_2_q & {4{in_1}};  // AND_Gate and_15, 4 bits wide
  and If0ThenSet1 (If0ThenSet1_out, not_12_out, not_11_out, not_10_out, not_9_out, not_8_out, not_7_out, not_6_out, not_5_out);
  Hex_Digit_Display hex_digit_display_1 (.value(and_15_out));  // open: dp
  Hex_Digit_Display hex_digit_display_2 (.value(and_14_out));  // open: dp

  // Notes on the sheet:
  //   SR Latch
  //   TRACK
endmodule
