// Logisim project volume.circ as structural Verilog: 1 circuit, main circuit Volume
module Volume (
);

  wire A_out, and_1_out, and_2_out, and_3_out, and_4_out, and_5_out, and_6_out, and_7_out, and_8_out,
       and_9_out, and_10_out, and_11_out, and_12_out, and_13_out, and_14_out, and_15_out, and_16_out, B_out,
       buffer_1_out, buffer_2_out, buffer_3_out, buffer_4_out, C_out, d_ff_1_q, d_ff_2_q, d_ff_3_q, d_ff_4_q,
       d_ff_5_q, d_ff_6_q, d_ff_7_q, d_ff_8_q, not_1_out, not_2_out, not_3_out, not_4_out, not_5_out,
       not_6_out, not_7_out, not_8_out, not_9_out, not_10_out, or_1_out, or_2_out, or_3_out, or_4_out,
       or_5_out, or_6_out, or_7_out, or_8_out, VOL_DOWN_out, VOL_UP_out;

  Button VOL_UP (.out(VOL_UP_out));
  Button VOL_DOWN (.out(VOL_DOWN_out));
  not not_1 (not_1_out, VOL_UP_out);
  not not_2 (not_2_out, VOL_DOWN_out);
  or A (A_out, not_1_out, VOL_DOWN_out);
  or B (B_out, VOL_UP_out, not_2_out);
  or C (C_out, VOL_UP_out, VOL_DOWN_out);
  not not_3 (not_3_out, A_out);
  buf buffer_1 (buffer_1_out, C_out);
  buf buffer_2 (buffer_2_out, buffer_1_out);
  buf buffer_3 (buffer_3_out, buffer_2_out);
  buf buffer_4 (buffer_4_out, buffer_3_out);
  and and_1 (and_1_out, not_3_out, B_out);
  and and_2 (and_2_out, A_out, d_ff_2_q);
  or or_1 (or_1_out, and_1_out, and_2_out);
  D_Flip_Flop d_ff_1 (.D(or_1_out), .clk(buffer_4_out), .Q(d_ff_1_q));  // open: Qn, preset, reset
  not not_4 (not_4_out, A_out);
  and and_3 (and_3_out, not_4_out, d_ff_1_q);
  and and_4 (and_4_out, A_out, d_ff_3_q);
  D_Flip_Flop d_ff_2 (.D(or_2_out), .clk(buffer_4_out), .Q(d_ff_2_q));  // open: Qn, preset, reset
  or or_2 (or_2_out, and_3_out, and_4_out);
  not not_5 (not_5_out, A_out);
  and and_5 (and_5_out, not_5_out, d_ff_2_q);
  and and_6 (and_6_out, A_out, d_ff_4_q);
  D_Flip_Flop d_ff_3 (.D(or_3_out), .clk(buffer_4_out), .Q(d_ff_3_q));  // open: Qn, preset, reset
  or or_3 (or_3_out, and_5_out, and_6_out);
  not not_6 (not_6_out, A_out);
  and and_7 (and_7_out, not_6_out, d_ff_3_q);
  and and_8 (and_8_out, A_out, d_ff_5_q);
  or or_4 (or_4_out, and_7_out, and_8_out);
  D_Flip_Flop d_ff_4 (.D(or_4_out), .clk(buffer_4_out), .Q(d_ff_4_q));  // open: Qn, preset, reset
  not not_7 (not_7_out, A_out);
  LedBar ledbar_1 (
    .led0(d_ff_1_q), .led1(d_ff_2_q), .led2(d_ff_3_q), .led3(d_ff_4_q), .led4(d_ff_5_q), .led5(d_ff_6_q),
    .led6(d_ff_7_q), .led7(d_ff_8_q));
  and and_9 (and_9_out, not_7_out, d_ff_4_q);
  and and_10 (and_10_out, A_out, d_ff_6_q);
  D_Flip_Flop d_ff_5 (.D(or_5_out), .clk(buffer_4_out), .Q(d_ff_5_q));  // open: Qn, preset, reset
  or or_5 (or_5_out, and_9_out, and_10_out);
  not not_8 (not_8_out, A_out);
  and and_11 (and_11_out, not_8_out, d_ff_5_q);
  and and_12 (and_12_out, A_out, d_ff_7_q);
  D_Flip_Flop d_ff_6 (.D(or_6_out), .clk(buffer_4_out), .Q(d_ff_6_q));  // open: Qn, preset, reset
  or or_6 (or_6_out, and_11_out, and_12_out);
  not not_9 (not_9_out, A_out);
  and and_13 (and_13_out, not_9_out, d_ff_6_q);
  and and_14 (and_14_out, A_out, d_ff_8_q);
  D_Flip_Flop d_ff_7 (.D(or_7_out), .clk(buffer_4_out), .Q(d_ff_7_q));  // open: Qn, preset, reset
  or or_7 (or_7_out, and_13_out, and_14_out);
  not not_10 (not_10_out, A_out);
  and and_15 (and_15_out, not_10_out, d_ff_7_q);
  and and_16 (and_16_out, A_out, B_out);
  or or_8 (or_8_out, and_15_out, and_16_out);
  D_Flip_Flop d_ff_8 (.D(or_8_out), .clk(buffer_4_out), .Q(d_ff_8_q));  // open: Qn, preset, reset

  // Notes on the sheet:
  //   Delay Buffer
  //   Common Data Load
  //   Combinational Circuit
endmodule
